# Fritzing sketch Interactive Drawing Robot Sketch (saved by Fritzing 0.9.3b)
breadboards: 1

parts:
  Part1 = Arduino Uno (Rev3)
  R1 = Resistor [tolerance=±5% resistance=3.3k package=THT]
  S1 = Pushbutton [package="[THT]"]
  R2 = Resistor [tolerance=±5% resistance=220 package=THT]
  R3 = Photocell (LDR) [package=THT]
  J1 = female pin header, 3 pins [form="♀ (female)" part_number="Stepper 1"]
  J2 = female pin header, 3 pins [form="♀ (female)" part_number="Stepper 2"]

nets:
  N1: Part1.A0, R2.Pin_1, R3.pin_1
  N2: Part1.D8, R1.Pin_1, S1.Pin_3, S1.Pin_4
  N3: Part1.D2, J2.pin3
  N4: Part1.D3_PWM, J2.pin2
  N5: Part1.D4, J1.pin3
  N6: Part1.D5_PWM, J1.pin2
  N7: Part1.5V, R1.Pin_0, R3.pin_0
  N8: Part1.GND, S1.Pin_1, S1.Pin_2, R2.Pin_0, J1.pin1, J2.pin1
